# Fritzing sketch acDimmer_ESP-12 (saved by Fritzing 0.9.1b)
circuit board: 7.19499cm x 3.87849cm
breadboards: 1

parts:
  4n25 = Optocoupler [part_number=4N25 package=THT]
  15k = Resistor [tolerance=±5% resistance=15k package=THT]
  1k = Resistor [tolerance=±5% resistance=1k package=THT]
  15k_2 = Resistor [tolerance=±5% resistance=15k package=THT]
  400V_Bridge = mystery part, 6 pins [chip_label=?]
  HV_AC = screw terminal, 4 pins
  MOC3021 = MOC3031-M [part_number=MOC3021 package=dil06]
  TIC206 = Basic FET N-Channel [part_number=TIC206 package="TO220 [THT]"]
  10k = Resistor [tolerance=±5% resistance=10k package=THT]
  Switch = Screw terminal - 2 pins [package=THT]
  470k = Resistor [tolerance=±5% resistance=470 package=THT]
  MSP-12 = IC, DIP package, 16 pins [chip_label=IC]
  Switch_2 = Screw terminal - 2 pins [package=THT]
  3_3v_Supply = mystery part, 8 pins [chip_label=?]

nets (from the pcb view):
  N1: 4n25.Pin_1, 400V_Bridge.pin1
  N2: 4n25.Pin_2, 400V_Bridge.pin3
  N3: 4n25.Pin_4, MOC3021.1, MSP-12.pin1, Switch_2.pin2, 3_3v_Supply.pin3
  N4: 4n25.Pin_5, 10k.Pin_1, MSP-12.pin14
  N5: 15k.Pin_0, 400V_Bridge.pin6
  N6: 15k.Pin_1, HV_AC.pin1, HV_AC.pin2, 3_3v_Supply.pin8
  N7: 1k.Pin_0, MOC3021.6
  N8: 1k.Pin_1, 15k_2.Pin_1, HV_AC.pin3, TIC206.drain, 3_3v_Supply.pin5
  N9: 15k_2.Pin_0, 400V_Bridge.pin4
  N10: HV_AC.pin4, TIC206.gate
  N11: MOC3021.2, 470k.Pin_1
  N12: MOC3021.4, TIC206.source
  N13: 10k.Pin_0, MSP-12.pin16, 3_3v_Supply.pin1
  N14: Switch.pin1, MSP-12.pin13
  N15: Switch.pin2, MSP-12.pin6
  N16: 470k.Pin_0, MSP-12.pin15
  N17: MSP-12.pin5, Switch_2.pin1
  N18: MSP-12.pin9, MSP-12.pin12

notes:
  0-X
  Load
  Mains
  +
  -
